// Logisim project 1.circ as structural Verilog: 1 circuit, main circuit main
module main (
);

  wire A, ABC_out, B, B_nC_nD_out, B_nD_out, BC_out, C, clock, D, f, g, go, nAB_out, nABC_out, nABD_out,
       not_1_out, not_2_out, not_3_out, not_4_out, not_5_out, Reset_out, t_ff_1_q, t_ff_2_q, t_ff_3_q,
       t_ff_4_q;

  not not_1 (not_1_out, A);
  not not_2 (not_2_out, C);
  not not_3 (not_3_out, D);
  not not_4 (not_4_out, A);
  not not_5 (not_5_out, D);
  and nABC (nABC_out, not_1_out, B, C);
  and nABD (nABD_out, not_1_out, D, B);
  and B_nC_nD (B_nC_nD_out, B, not_2_out, not_3_out);
  and ABC (ABC_out, C, B, A);
  and B_nD (B_nD_out, B, not_5_out);
  and nAB (nAB_out, not_4_out, B);
  and BC (BC_out, B, C);
  or or_1 (f, nABC_out, nABD_out, B_nC_nD_out, ABC_out);
  or or_2 (g, B_nD_out, nAB_out, BC_out);
  Clock clock_1 (.out(clock));
  // Probe on {A, B, C, D}
  T_Flip_Flop t_ff_1 (.clk(clock), .T(1'b1), .Q(t_ff_1_q), .Qn(D), .preset(Reset_out), .en(go));  // open: reset
  // Probe on {A, B, C, D}
  // Probe on f
  T_Flip_Flop t_ff_2 (.clk(t_ff_1_q), .T(1'b1), .Q(t_ff_2_q), .Qn(C), .preset(Reset_out));  // open: reset, en
  // Probe on g
  TTY #(.rows(1), .cols(18)) tty_1 (.data({6'b011000, f}), .clk(clock), .we(go), .clr(Reset_out));
  T_Flip_Flop t_ff_3 (.clk(t_ff_2_q), .T(1'b1), .Q(t_ff_3_q), .Qn(B), .preset(Reset_out));  // open: reset, en
  TTY #(.rows(1), .cols(18)) tty_2 (.data({6'b011000, g}), .clk(clock), .we(go), .clr(Reset_out));
  T_Flip_Flop t_ff_4 (.clk(t_ff_3_q), .T(1'b1), .Q(t_ff_4_q), .Qn(A), .preset(Reset_out));  // open: reset, en
  Button Reset (.out(Reset_out));
  T_Flip_Flop t_ff_5 (.clk(t_ff_4_q), .T(1'b1), .Q(go), .preset(Reset_out));  // open: Qn, reset, en

  // Notes on the sheet:
  //   FUNTION F
  //   FUNCTION G
  //   test case
  //   0000111100001011
  //   0000111100001011
endmodule
