// Logisim project 2.circ as structural Verilog: 1 circuit, main circuit main
module main (
);

  wire A, and_1_out, and_2_out, and_3_out, and_4_out, B, C, clock_1_out, D, f, go, not_3_out, not_4_out,
       Reset_out, t_ff_1_q, t_ff_2_q, t_ff_3_q, t_ff_4_q;

  // NOT_Gate not_1 has open pins: in=A, out=open
  // NOT_Gate not_2 has open pins: in=B, out=open
  not not_3 (not_3_out, D);
  not not_4 (not_4_out, C);
  and and_1 (and_1_out, B, not_4_out, not_3_out);
  and and_2 (and_2_out, A, not_4_out, not_3_out);
  and and_3 (and_3_out, B, C, D);
  and and_4 (and_4_out, A, C, D);
  or or_1 (f, and_1_out, and_2_out, and_3_out, and_4_out);
  // Probe on {A, B, C, D}
  Clock clock_1 (.out(clock_1_out));
  T_Flip_Flop t_ff_1 (.clk(clock_1_out), .T(1'b1), .Q(t_ff_1_q), .Qn(D), .preset(Reset_out), .en(go));  // open: reset
  // Probe on f
  T_Flip_Flop t_ff_2 (.clk(t_ff_1_q), .T(1'b1), .Q(t_ff_2_q), .Qn(C), .preset(Reset_out));  // open: reset, en
  TTY #(.rows(1), .cols(18)) tty_1 (.data({6'b011000, f}), .clk(clock_1_out), .we(go), .clr(Reset_out));
  T_Flip_Flop t_ff_3 (.clk(t_ff_2_q), .T(1'b1), .Q(t_ff_3_q), .Qn(B), .preset(Reset_out));  // open: reset, en
  T_Flip_Flop t_ff_4 (.clk(t_ff_3_q), .T(1'b1), .Q(t_ff_4_q), .Qn(A), .preset(Reset_out));  // open: reset, en
  Button Reset (.out(Reset_out));
  T_Flip_Flop t_ff_5 (.clk(t_ff_4_q), .T(1'b1), .Q(go), .preset(Reset_out));  // open: Qn, reset, en

  // Notes on the sheet:
  //   000010011001d00d
endmodule
