// Logisim project 3.circ as structural Verilog: 1 circuit, main circuit main
module main (
);

  wire A, B, C, clock_1_out, D, E, F, go, Reset_out, t_ff_1_q, t_ff_2_q, t_ff_3_q, t_ff_4_q, t_ff_5_q,
       t_ff_6_q, X0, X1, X2;

  // Probe on {A, B, C, D, E, F}
  BitAdder #(.width(1)) bitadder_1 (.in0(A), .in1(B), .in2(C), .in3(D), .in4(E), .in5(F), .out({X2, X1, X0}));
  // Probe on {X2, X1, X0}
  TTY #(.rows(1), .cols(65)) tty_1 (.data({4'b0110, X2, X1, X0}), .clk(clock_1_out), .we(go), .clr(Reset_out));
  Clock clock_1 (.out(clock_1_out));
  T_Flip_Flop t_ff_1 (.clk(t_ff_2_q), .T(1'b1), .Q(t_ff_1_q), .Qn(E), .preset(Reset_out));  // open: reset, en
  T_Flip_Flop t_ff_2 (.clk(clock_1_out), .T(1'b1), .Q(t_ff_2_q), .Qn(F), .preset(Reset_out), .en(go));  // open: reset
  T_Flip_Flop t_ff_3 (.clk(t_ff_1_q), .T(1'b1), .Q(t_ff_3_q), .Qn(D), .preset(Reset_out));  // open: reset, en
  T_Flip_Flop t_ff_4 (.clk(t_ff_3_q), .T(1'b1), .Q(t_ff_4_q), .Qn(C), .preset(Reset_out));  // open: reset, en
  T_Flip_Flop t_ff_5 (.clk(t_ff_4_q), .T(1'b1), .Q(t_ff_5_q), .Qn(B), .preset(Reset_out));  // open: reset, en
  T_Flip_Flop t_ff_6 (.clk(t_ff_5_q), .T(1'b1), .Q(t_ff_6_q), .Qn(A), .preset(Reset_out));  // open: reset, en
  Button Reset (.out(Reset_out));
  T_Flip_Flop t_ff_7 (.clk(t_ff_6_q), .T(1'b1), .Q(go), .preset(Reset_out));  // open: Qn, reset, en

  // Notes on the sheet:
  //   test case
  //   0112122312232334122323342334344512232334233434452334344534454556
endmodule
