// Logisim project 5.circ as structural Verilog: 1 circuit, main circuit main
module main (
);

  wire A, and_1_out, B, C, clock_1_out, f, go, not_2_out, not_3_out, or_1_out, Reset_out, t_ff_1_q, t_ff_2_q,
       t_ff_3_q;

  // NOT_Gate not_1 has open pins: in=B, out=open
  not not_2 (not_2_out, A);
  not not_3 (not_3_out, C);
  and and_1 (and_1_out, not_2_out, B);
  or or_1 (or_1_out, not_2_out, B);
  Multiplexer multiplexer_1 (.in0(and_1_out), .in1(or_1_out), .out(f), .sel(not_3_out));  // open: en
  // Probe on {A, B, C}
  Clock clock_1 (.out(clock_1_out));
  // Probe on f
  T_Flip_Flop t_ff_1 (.clk(clock_1_out), .T(1'b1), .Q(t_ff_1_q), .Qn(C), .preset(Reset_out), .en(go));  // open: reset
  T_Flip_Flop t_ff_2 (.clk(t_ff_1_q), .T(1'b1), .Q(t_ff_2_q), .Qn(B), .preset(Reset_out));  // open: reset, en
  TTY #(.rows(1), .cols(10)) tty_1 (.data({6'b011000, f}), .clk(clock_1_out), .we(go), .clr(Reset_out));
  T_Flip_Flop t_ff_3 (.clk(t_ff_2_q), .T(1'b1), .Q(t_ff_3_q), .Qn(A), .preset(Reset_out));  // open: reset, en
  Button Reset (.out(Reset_out));
  T_Flip_Flop t_ff_4 (.clk(t_ff_3_q), .T(1'b1), .Q(go), .preset(Reset_out));  // open: Qn, reset, en

  // Notes on the sheet:
  //   10110010
endmodule
