// Logisim project 7.circ as structural Verilog: 1 circuit, main circuit main
module main (
);

  wire A0, A1, A2, adder_1_cout, C0, C1, C2, C3, C_prime_0, C_prime_1, C_prime_2, C_prime_3, clock_1_out,
       comparator_1_eq, comparator_2_eq, comparator_3_eq, comparator_4_eq, comparator_5_eq, comparator_6_eq,
       comparator_7_eq, comparator_8_eq, D0, D1, D2, D3, D4, D5, D6, D7, go, not_1_out, not_2_out, not_3_out,
       not_4_out, not_5_out, not_6_out, not_7_out, not_8_out, P0, P1, P2, Reset_out, t_ff_1_q, t_ff_2_q,
       t_ff_3_q, t_ff_4_q, t_ff_5_q, t_ff_6_q, xor_1_out, xor_2_out, xor_3_out, xor_4_out, Z0, Z1, Z2, Z3,
       Z4, Z5, Z6, Z7;
  wire [0:0] multiplexer_13_out;
  wire [3:0] adder_1_out, adder_2_out, multiplexer_9_out, multiplexer_10_out, multiplexer_11_out,
       multiplexer_12_out, position;

  // Probe on D7
  // Probe on D6
  // Probe on D4
  // Probe on D5
  // Probe on D3
  // Probe on D2
  Comparator #(.width(4)) comparator_1 (.a(position), .b(4'b0011), .eq(comparator_1_eq));  // open: gt, lt
  Comparator #(.width(4)) comparator_2 (.a(position), .b(4'b0101), .eq(comparator_2_eq));  // open: gt, lt
  Comparator #(.width(4)) comparator_3 (.a(position), .b(4'b0110), .eq(comparator_3_eq));  // open: gt, lt
  Comparator #(.width(4)) comparator_4 (.a(position), .b(4'b0111), .eq(comparator_4_eq));  // open: gt, lt
  Comparator #(.width(4)) comparator_5 (.a(position), .b(4'b1001), .eq(comparator_5_eq));  // open: gt, lt
  Comparator #(.width(4)) comparator_6 (.a(position), .b(4'b1010), .eq(comparator_6_eq));  // open: gt, lt
  Comparator #(.width(4)) comparator_7 (.a(position), .b(4'b1011), .eq(comparator_7_eq));  // open: gt, lt
  Comparator #(.width(4)) comparator_8 (.a(position), .b(4'b1100), .eq(comparator_8_eq));  // open: gt, lt
  // Probe on D1
  // Probe on D0
  not not_1 (not_1_out, D0);
  not not_2 (not_2_out, D1);
  not not_3 (not_3_out, D2);
  not not_4 (not_4_out, D3);
  not not_5 (not_5_out, D4);
  not not_6 (not_6_out, D5);
  not not_7 (not_7_out, D6);
  not not_8 (not_8_out, D7);
  // Probe on C_prime_0
  xor odd_parity_1 (C_prime_0, D0, D1, D3, D4, D6);
  xor odd_parity_2 (C_prime_1, D0, D2, D3, D5, D6);
  xor odd_parity_3 (C_prime_2, D1, D2, D3, D7);
  xor odd_parity_4 (C_prime_3, D4, D5, D6, D7);
  Multiplexer multiplexer_1 (.in0(D0), .in1(not_1_out), .out(Z0), .sel(comparator_1_eq));  // open: en
  Multiplexer multiplexer_2 (.in0(D1), .in1(not_2_out), .out(Z1), .sel(comparator_2_eq));  // open: en
  Multiplexer multiplexer_3 (.in0(D2), .in1(not_3_out), .out(Z2), .sel(comparator_3_eq));  // open: en
  Multiplexer multiplexer_4 (.in0(D3), .in1(not_4_out), .out(Z3), .sel(comparator_4_eq));  // open: en
  Multiplexer multiplexer_5 (.in0(D4), .in1(not_5_out), .out(Z4), .sel(comparator_5_eq));  // open: en
  Multiplexer multiplexer_6 (.in0(D5), .in1(not_6_out), .out(Z5), .sel(comparator_6_eq));  // open: en
  Multiplexer multiplexer_7 (.in0(D6), .in1(not_7_out), .out(Z6), .sel(comparator_7_eq));  // open: en
  Multiplexer multiplexer_8 (.in0(D7), .in1(not_8_out), .out(Z7), .sel(comparator_8_eq));  // open: en
  Clock clock_1 (.out(clock_1_out));
  xor xor_1 (xor_1_out, C_prime_0, C0);
  xor xor_2 (xor_2_out, C_prime_1, C1);
  xor xor_3 (xor_3_out, C_prime_2, C2);
  xor xor_4 (xor_4_out, C_prime_3, C3);
  T_Flip_Flop t_ff_1 (.clk(clock_1_out), .T(1'b1), .Q(t_ff_1_q), .Qn(P0), .preset(Reset_out), .en(go));  // open: reset
  Multiplexer #(.width(4)) multiplexer_9 (
    .in0(4'b0000), .in1(4'b0001), .out(multiplexer_9_out), .sel(xor_1_out));  // open: en
  Multiplexer #(.width(4)) multiplexer_10 (
    .in0(4'b0000), .in1(4'b0010), .out(multiplexer_10_out), .sel(xor_2_out));  // open: en
  Multiplexer #(.width(4)) multiplexer_11 (
    .in0(4'b0000), .in1(4'b0100), .out(multiplexer_11_out), .sel(xor_3_out));  // open: en
  Multiplexer #(.width(4)) multiplexer_12 (
    .in0(4'b0000), .in1(4'b1000), .out(multiplexer_12_out), .sel(xor_4_out));  // open: en
  Multiplexer #(.select(3), .disabled(0), .enable("false")) multiplexer_13 (
    .in0(Z7), .in1(Z6), .in2(Z5), .in3(Z4), .in4(Z3), .in5(Z2), .in6(Z1), .in7(Z0),
    .out(multiplexer_13_out[0]), .sel({P2, P1, P0}));
  T_Flip_Flop t_ff_2 (.clk(t_ff_1_q), .T(1'b1), .Q(t_ff_2_q), .Qn(P1), .preset(Reset_out));  // open: reset, en
  TTY #(.cols(8)) tty_1 (.data({6'b011000, multiplexer_13_out[0]}), .clk(clock_1_out), .we(go), .clr(Reset_out));
  T_Flip_Flop t_ff_3 (.clk(t_ff_4_q), .T(1'b1), .Q(t_ff_3_q), .Qn(A0), .preset(Reset_out));  // open: reset, en
  T_Flip_Flop t_ff_4 (.clk(t_ff_2_q), .T(1'b1), .Q(t_ff_4_q), .Qn(P2), .preset(Reset_out));  // open: reset, en
  // Probe on {D7, D6, D5, D4, C3, D3, D2, D1, C2, D0, C1, C0}
  ROM #(.addrWidth(3), .dataWidth(12)) rom_1 (
    .addr({A2, A1, A0}), .data({D7, D6, D5, D4, C3, D3, D2, D1, C2, D0, C1, C0}));  // open: sel
  Adder #(.width(4)) adder_1 (
    .a(multiplexer_9_out), .b(multiplexer_10_out), .out(adder_1_out), .cout(adder_1_cout));  // open: cin
  Adder #(.width(4)) adder_2 (
    .a(multiplexer_11_out), .b(multiplexer_12_out), .out(adder_2_out), .cin(adder_1_cout));  // open: cout
  T_Flip_Flop t_ff_5 (.clk(t_ff_3_q), .T(1'b1), .Q(t_ff_5_q), .Qn(A1), .preset(Reset_out));  // open: reset, en
  // Probe on position
  Adder #(.width(4)) adder_3 (.a(adder_1_out), .b(adder_2_out), .out(position));  // open: cin, cout
  T_Flip_Flop t_ff_6 (.clk(t_ff_5_q), .T(1'b1), .Q(t_ff_6_q), .Qn(A2), .preset(Reset_out));  // open: reset, en
  T_Flip_Flop t_ff_7 (.clk(t_ff_6_q), .T(1'b1), .Q(go), .preset(Reset_out));  // open: Qn, reset, en
  Button Reset (.out(Reset_out));

  // Notes on the sheet:
  //   11
  //   12
  //   9
  //   10
  //   7
  //   6
  //   3
  //   5
  //   contents of rom_1 (hex, n*v repeats v):
  //   d7 788 a75 a74 275 b75 f75 a77
  //   00101011
  //   01110000
  //   10101111
  //   10101111
  //   10101111
  //   10101111
  //   11111111
  //   10101111
endmodule
