// Logisim project 2.circ as structural Verilog: 1 circuit, main circuit main
module main (
);

  wire _4_Counter_carry, CLK, clock_1_out, go, or_1_out, Q, R, Reset_out, RQ_out, S, S_nQ_out, t_ff_1_qn;
  wire [3:0] _4_Counter_q;

  and RQ (RQ_out, Q, R);
  and S_nQ (S_nQ_out, S, t_ff_1_qn);
  or or_1 (or_1_out, RQ_out, S_nQ_out);
  T_Flip_Flop t_ff_1 (.clk(CLK), .T(or_1_out), .Q(Q), .Qn(t_ff_1_qn));  // open: preset, reset, en
  TTY #(.rows(1), .cols(12)) tty_1 (.data({6'b011000, Q}), .clk(CLK), .we(go), .clr(Reset_out));
  Button Reset (.out(Reset_out));
  and and_1 (CLK, clock_1_out, go);
  Clock clock_1 (.out(clock_1_out));
  // Probe on _4_Counter_q
  Counter #(.width(4), .max('hc)) _4_Counter (
    .Q(_4_Counter_q), .carry(_4_Counter_carry), .clk(CLK), .clr(Reset_out));  // open: load, D, count
  not not_1 (go, _4_Counter_carry);
  // Probe on S
  ROM #(.addrWidth(4), .dataWidth(2)) rom_1 (.addr(_4_Counter_q), .data({R, S}));  // open: sel
  // Probe on R

  // Notes on the sheet:
  //   001111000011
  //   contents of rom_1 (hex, n*v repeats v):
  //   0 1 0 1 0 2 0 2 0 1
endmodule
