// Logisim project 4.circ as structural Verilog: 3 circuits, main circuit main
module main (
);

  wire and_1_out, and_2_out, and_3_out, Carry, CLK, clock_1_out, counter_1_carry, D0, D1, D2, D3, Enable,
       Load, multiplexer_1_out, multiplexer_2_out, multiplexer_3_out, multiplexer_4_out, not_1_out, Q0, Q1,
       Q2, Q3, xor_1_c, xor_2_c, xor_3_c, xor_4_c;
  wire [5:1] counter_1_q;

  and and_1 (and_1_out, Enable, Q0);
  and and_2 (and_2_out, and_1_out, Q1);
  and and_3 (and_3_out, and_2_out, Q2);
  and and_4 (Carry, and_3_out, Q3);
  XOR xor_1 (.A(Q0), .B(Enable), .C(xor_1_c));
  XOR xor_2 (.A(Q1), .B(and_1_out), .C(xor_2_c));
  XOR xor_3 (.A(Q2), .B(and_2_out), .C(xor_3_c));
  XOR xor_4 (.A(Q3), .B(and_3_out), .C(xor_4_c));
  Multiplexer multiplexer_1 (.in0(xor_1_c), .in1(D0), .out(multiplexer_1_out), .sel(Load));  // open: en
  Multiplexer multiplexer_2 (.in0(xor_2_c), .in1(D1), .out(multiplexer_2_out), .sel(Load));  // open: en
  Multiplexer multiplexer_3 (.in0(xor_3_c), .in1(D2), .out(multiplexer_3_out), .sel(Load));  // open: en
  Multiplexer multiplexer_4 (.in0(xor_4_c), .in1(D3), .out(multiplexer_4_out), .sel(Load));  // open: en
  Flip_Flop flip_flop_1 (.CLK(CLK), .I(multiplexer_1_out), .Q(Q0));  // open: nQ
  Flip_Flop flip_flop_2 (.CLK(CLK), .I(multiplexer_2_out), .Q(Q1));  // open: nQ
  Flip_Flop flip_flop_3 (.CLK(CLK), .I(multiplexer_3_out), .Q(Q2));  // open: nQ
  Flip_Flop flip_flop_4 (.CLK(CLK), .I(multiplexer_4_out), .Q(Q3));  // open: nQ
  and and_5 (CLK, clock_1_out, not_1_out);
  Clock clock_1 (.out(clock_1_out));
  Counter #(.width(6), .max('h24)) counter_1 (
    .Q({counter_1_q[5], Load, D3, counter_1_q[2:1], D0}), .carry(counter_1_carry), .clk(CLK));  // open: load, D, count, clr
  not not_1 (not_1_out, counter_1_carry);
  TTY #(.rows(1), .cols(37)) tty_1 (.data({2'b10, Carry, Q3, Q2, Q1, Q0}), .clk(CLK));  // open: we, clr
  not not_2 (Enable, counter_1_q[5]);
  or or_1 (D1, Enable, counter_1_q[1]);
  or or_2 (D2, counter_1_q[2], Load);

  // Notes on the sheet:
  //   A
  //   B
  //   @ABCDEFGHIJKLMN_@FGFGFGFGN_N_N_N0000
endmodule

module Flip_Flop (
  input  CLK,
  input  I,
  output Q,
  output nQ
);

  wire and_1_out, and_2_out, not_1_out, or_1_out;

  not not_1 (not_1_out, I);
  and and_1 (and_1_out, Q, not_1_out);
  or or_1 (or_1_out, and_1_out, and_2_out);
  and and_2 (and_2_out, I, nQ);
  T_Flip_Flop t_ff_1 (.clk(CLK), .T(or_1_out), .Q(Q), .Qn(nQ));  // open: preset, reset, en
endmodule

module XOR (
  input  A,
  input  B,
  output C
);

  wire and_1_out, and_2_out, not_1_out, not_2_out;

  not not_1 (not_1_out, B);
  not not_2 (not_2_out, A);
  and and_1 (and_1_out, A, not_1_out);
  or or_1 (C, and_1_out, and_2_out);
  and and_2 (and_2_out, not_2_out, B);
endmodule
