// Logisim project 5.circ as structural Verilog: 2 circuits, main circuit main
module main (
);

  wire _4_Counter_carry, _8_Counter_carry, A, and_1_out, and_2_out, and_3_out, and_4_out, and_5_out, B, CLK,
       clock_1_out, go, nA, nA_nBW_out, nB, not_1_out, or_1_out, or_2_out, Q, Reset_out, w, xor_1_out,
       xor_2_out;
  wire [1:0] _4_Counter_q;
  wire [3:0] _8_Counter_q;

  not not_1 (not_1_out, w);
  and and_1 (and_1_out, nA, nB);
  and and_2 (and_2_out, not_1_out, A);
  and nA_nBW (nA_nBW_out, nA, nB, w);
  and and_3 (and_3_out, nA, B, not_1_out);
  and and_4 (and_4_out, A, B, w);
  and and_5 (and_5_out, A, nB, not_1_out);
  or or_1 (or_1_out, and_1_out, and_2_out);
  xor xor_1 (xor_1_out, A, or_1_out);
  xor xor_2 (xor_2_out, B, or_2_out);
  or or_2 (or_2_out, nA_nBW_out, and_3_out, and_4_out, and_5_out);
  T_Flip_Flop t_ff_1 (.clk(CLK), .T(xor_1_out), .Q(A), .Qn(nA));  // open: preset, reset, en
  T_Flip_Flop t_ff_2 (.clk(CLK), .T(xor_2_out), .Q(B), .Qn(nB));  // open: preset, reset, en
  and and_6 (Q, A, B);
  TTY #(.rows(1), .cols(33)) tty_1 (.data({6'b011000, Q}), .clk(CLK), .we(go), .clr(Reset_out));
  // Probe on _4_Counter_q
  Counter #(.width(2), .max('h3)) _4_Counter (
    .Q(_4_Counter_q), .carry(_4_Counter_carry), .clk(CLK), .clr(Reset_out));  // open: load, D, count
  and and_7 (CLK, clock_1_out, go);
  Clock clock_1 (.out(clock_1_out));
  Counter #(.width(4), .max('h8)) _8_Counter (
    .Q(_8_Counter_q), .carry(_8_Counter_carry), .clk(_4_Counter_carry), .clr(Reset_out));  // open: load, D, count
  // Probe on _8_Counter_q
  not not_2 (go, _8_Counter_carry);
  Button Reset (.out(Reset_out));
  // Probe on w
  BitSelector #(.width(4)) bitselector_1 (.in(_8_Counter_q), .out(w), .sel(_4_Counter_q));

  // Notes on the sheet:
  //   A
  //   B
  //   0010100000001000101000000100001
endmodule

module Flip_Flop (
  input  CLK,
  input  I,
  output Q,
  output nQ
);

  wire and_1_out, and_2_out, not_1_out, or_1_out;

  not not_1 (not_1_out, I);
  and and_1 (and_1_out, Q, not_1_out);
  or or_1 (or_1_out, and_1_out, and_2_out);
  and and_2 (and_2_out, I, nQ);
  T_Flip_Flop t_ff_1 (.clk(CLK), .T(or_1_out), .Q(Q), .Qn(nQ));  // open: preset, reset, en
endmodule
