// Logisim project 7.circ as structural Verilog: 1 circuit, main circuit main
module main (
);

  wire _5_Counter_carry, A, A_prime, and_1_out, and_2_out, and_3_out, and_4_out, and_5_out, and_6_out,
       and_7_out, and_8_out, and_9_out, and_10_out, and_11_out, and_12_out, and_13_out, and_14_out,
       and_15_out, and_16_out, B, B_prime, C, C_prime, CLK, clock_1_out, D, D_prime, go, nA, nB, nC, nD, nw,
       p, Reset_out, w;
  wire [2:0] _5_Counter_q;
  wire [5:0] _64_Counter_q;

  not not_1 (nw, w);
  and and_1 (and_1_out, nA, D, w);
  and and_2 (and_2_out, nA, B, nD);
  and and_3 (and_3_out, B, w);
  and and_4 (and_4_out, A, nB, nC, nw);
  and and_5 (and_5_out, A, nD, w);
  and and_6 (and_6_out, A, C, w);
  and and_7 (and_7_out, nA, nD, nw);
  and and_8 (and_8_out, B, nD, w);
  and and_9 (and_9_out, nA, nB, D);
  and and_10 (and_10_out, C, D, nw);
  and and_11 (and_11_out, A, C, nD);
  and and_12 (and_12_out, A, nC, D, w);
  and and_13 (and_13_out, A, nB, nC, D);
  and and_14 (and_14_out, nD, w);
  and and_15 (and_15_out, C, w);
  and and_16 (and_16_out, nC, D, nw);
  or or_1 (A_prime, and_1_out, and_2_out, and_3_out, and_4_out, and_5_out, and_6_out);
  or or_2 (B_prime, and_7_out, and_8_out, and_9_out, and_10_out);
  or or_3 (C_prime, and_11_out, and_12_out, and_13_out);
  or or_4 (D_prime, and_14_out, and_15_out, and_16_out);
  D_Flip_Flop u_A (.clk(CLK), .D(A_prime), .Q(A), .Qn(nA));  // open: preset, en, reset
  D_Flip_Flop A_2 (.clk(CLK), .D(B_prime), .Q(B), .Qn(nB));  // open: preset, en, reset
  D_Flip_Flop u_C (.clk(CLK), .D(C_prime), .Q(C), .Qn(nC));  // open: preset, en, reset
  D_Flip_Flop u_D (.clk(CLK), .D(D_prime), .Q(D), .Qn(nD));  // open: preset, en, reset
  // Probe on p
  TTY #(.rows(33), .cols(5)) tty_1 (.data({6'b011000, p}), .clk(CLK), .we(go), .clr(Reset_out));
  Button Reset (.out(Reset_out));
  // Probe on w
  and and_17 (p, nA, nB, C, nD);
  nand nand_1 (go, _64_Counter_q[0], _64_Counter_q[5]);
  // Probe on _5_Counter_q
  Counter #(.width(3), .max('h4)) _5_Counter (
    .Q(_5_Counter_q), .carry(_5_Counter_carry), .clk(CLK), .clr(Reset_out));  // open: load, D, count
  and and_18 (CLK, clock_1_out, go);
  Clock clock_1 (.out(clock_1_out));
  // Probe on _64_Counter_q
  Counter #(.width(6), .max('h3f), .trigger("falling")) _64_Counter (
    .Q(_64_Counter_q), .clk(_5_Counter_carry), .clr(Reset_out));  // open: load, D, count, carry
  BitSelector #(.width(6)) bitselector_1 (.in(_64_Counter_q), .out(w), .sel(_5_Counter_q));

  // Notes on the sheet:
  //   1  3
  //   1  5
  //   1  6
  //   1  9
  //   1   10
  //   1  12
  //   1  15
  //   1  18
  //   1  20
  //   1  23
  //   1  24
  //   1 27
  //   1  29
  //   1  30
  //   1  0
  //   1  17
  //   24 Gates
endmodule
