// Logisim project 8.circ as structural Verilog: 1 circuit, main circuit main
module main (
);

  wire _4_Counter_carry, A, A_nBS1_out, A_nBS2_out, AS1_out, B, B_nC_nS1_nS2_out, B_nCS2_out, BC_nS1_nS2_out,
       BCS2_out, BS1_out, C, CLK, clock_1_out, clock_2_out, CS1_out, go, I5, I10, I25, nA_nBS2_out,
       nA_nC_nS1_nS2_out, nBC_nS1_out, nBCS2_out, not_2_out, not_3_out, not_4_out, not_5_out, not_6_out, O5,
       O10, OM, or_1_out, or_2_out, or_3_out, Reset_out;
  wire [4:0] _4_Counter_q;

  TTY #(.rows(1), .cols(33)) tty_1 (.data({4'b1000, OM, O10, O5}), .clk(CLK), .we(go), .clr(Reset_out));
  Button Reset (.out(Reset_out));
  // Probe on _4_Counter_q
  Counter #(.width(5), .max('h1f)) _4_Counter (
    .Q(_4_Counter_q), .carry(_4_Counter_carry), .clk(CLK), .clr(Reset_out));  // open: load, D, count
  and and_1 (CLK, clock_1_out, go);
  Clock clock_1 (.out(clock_1_out));
  not not_1 (go, _4_Counter_carry);
  ROM #(.addrWidth(5), .dataWidth(3)) rom_1 (.addr(_4_Counter_q), .data({I25, I10, I5}));  // open: sel
  // Probe on I5
  // Probe on I25
  // Probe on I10
  not not_2 (not_2_out, I25);
  not not_3 (not_3_out, I10);
  not not_4 (not_4_out, A);
  not not_5 (not_5_out, B);
  not not_6 (not_6_out, C);
  and BC_nS1_nS2 (BC_nS1_nS2_out, B, C, not_2_out, not_3_out);
  and B_nCS2 (B_nCS2_out, B, not_6_out, I10);
  and nA_nBS2 (nA_nBS2_out, not_4_out, not_5_out, I10);
  and nBC_nS1 (nBC_nS1_out, not_5_out, C, not_2_out);
  and B_nC_nS1_nS2 (B_nC_nS1_nS2_out, B, not_6_out, not_2_out, not_3_out);
  and nA_nC_nS1_nS2 (nA_nC_nS1_nS2_out, not_4_out, not_6_out, not_2_out, not_3_out);
  and nBCS2 (nBCS2_out, not_5_out, C, I10);
  and BCS2 (BCS2_out, B, C, I10);
  and CS1 (CS1_out, C, I25);
  and A_nBS2 (A_nBS2_out, A, not_5_out, I10);
  and A_nBS1 (A_nBS1_out, A, not_5_out, I25);
  and AS1 (AS1_out, A, I25);
  and BS1 (BS1_out, B, I25);
  Clock clock_2 (.out(clock_2_out));
  or or_1 (or_1_out, BC_nS1_nS2_out, B_nCS2_out);
  or or_2 (or_2_out, nA_nBS2_out, nBC_nS1_out, B_nC_nS1_nS2_out);
  or or_3 (or_3_out, nA_nC_nS1_nS2_out, nBCS2_out);
  or or_4 (OM, A, I25, BCS2_out);
  or or_5 (O5, CS1_out, A_nBS2_out, A_nBS1_out);
  or or_6 (O10, AS1_out, BS1_out);
  D_Flip_Flop u_A (.clk(clock_2_out), .D(or_1_out), .Q(A));  // open: Qn, preset, en, reset
  D_Flip_Flop u_B (.clk(clock_2_out), .D(or_2_out), .Q(B));  // open: Qn, preset, en, reset
  D_Flip_Flop u_C (.clk(clock_2_out), .D(or_3_out), .Q(C));  // open: Qn, preset, en, reset

  // Notes on the sheet:
  //   24 Gates
  //   D@@@@D@@@D@@E@E@F@@G@@G@F@@E@@@
  //   contents of rom_1 (hex, n*v repeats v):
  //   4 6*1 2 1 1 2 2 2 1 4 2 4 2 2 4 1 2 4 2 4 2 2 2 1 1 1 2
endmodule
