// Logisim project 9.circ as structural Verilog: 1 circuit, main circuit main
module main (
);

  wire A0, A1, A2, A3, A4, B0, B1, B2, B3, B4, C0, c0_t, C1, c1_t, C2, c2_t, C3, c3_t, C4, c4_t, C5,
       clock_1_out, clock_2_out, g0, g1, g2, g3, g4, go, HCLK, not_1_out, o0, o1, o2, o3, o4, p0, p0c0_out,
       p1, p1g0_out, p1p0c0_out, p2, p2g1_out, p2p1g0_out, p2p1p0c0_out, p3, p3g2_out, p3p2g1_out,
       p3p2p1g0_out, p3p2p1p0c0_out, p4, p4g3_out, p4p3g2_out, p4p3p2g1_out, p4p3p2p1g0_out,
       p4p3p2p1p0c0_out, q0, q1, reset, s0_t, s1_t, s2, s3, s4;
  wire [2:0] multiplexer_1_out;
  wire [4:0] not_3_out;
  wire [6:1] counter_1_q;

  // Probe on {C5, C4, C3}
  // Probe on {C2, C1, C0}
  Multiplexer #(.width(3)) multiplexer_1 (
    .in0({C5, C4, C3}), .in1({C2, C1, C0}), .out(multiplexer_1_out), .sel(HCLK));  // open: en
  // Probe on multiplexer_1_out
  // Probe on {4'b0110, multiplexer_1_out}
  TTY #(.rows(32), .cols(2)) tty_1 (.data({4'b0110, multiplexer_1_out}), .clk(clock_1_out), .we(go), .clr(reset));
  Clock clock_1 (.out(clock_1_out));
  // Probe on {A4, A3, A2, A1, A0, c0_t}
  // Probe on {B4, B3, B2, B1, B0}
  // Probe on q1
  Counter #(.width(7), .max('h7f), .ongoal("stay")) counter_1 (
    .Q({counter_1_q, HCLK}), .clk(clock_2_out), .clr(reset));  // open: load, D, count, carry
  Clock clock_2 (.out(clock_2_out));
  // Probe on q0
  not not_1 (not_1_out, HCLK);
  Button u_Reset (.out(reset));
  Random #(.width(13), .seed(34573)) random_1 (
    .clk(not_1_out), .next(go), .out({B4, B3, B2, B1, B0, A4, A3, A2, A1, A0, c0_t, q1, q0}), .clr(reset));
  not not_2 (go, counter_1_q[6]);
  or or_1 (o0, B0, A0);
  and and_1 (g0, A0, B0);
  or or_2 (o1, B1, A1);
  and and_2 (g1, A1, B1);
  or or_3 (o2, B2, A2);
  and and_3 (g2, A2, B2);
  or or_4 (o3, B3, A3);
  and and_4 (g3, A3, B3);
  or or_5 (o4, B4, A4);
  and and_5 (g4, A4, B4);
  xor xor_1 (p0, A0, B0);
  xor xor_2 (s0_t, p0, c0_t);
  xor xor_3 (p1, A1, B1);
  xor xor_4 (s1_t, p1, c1_t);
  xor xor_5 (p2, A2, B2);
  xor xor_6 (s2, p2, c2_t);
  xor xor_7 (p3, A3, B3);
  xor xor_8 (s3, p3, c3_t);
  xor xor_9 (p4, A4, B4);
  xor xor_10 (s4, p4, c4_t);
  or or_6 (c1_t, g0, p0c0_out);
  and p0c0 (p0c0_out, c0_t, p0);
  and p1g0 (p1g0_out, g0, p1);
  and p1p0c0 (p1p0c0_out, c0_t, p0, p1);
  and p2g1 (p2g1_out, g1, p2);
  and p2p1g0 (p2p1g0_out, g0, p2, p1);
  and p2p1p0c0 (p2p1p0c0_out, c0_t, p0, p1, p2);
  or or_7 (c2_t, g1, p1g0_out, p1p0c0_out);
  or or_8 (c3_t, g2, p2g1_out, p2p1g0_out, p2p1p0c0_out);
  and p3g2 (p3g2_out, g2, p3);
  and p3p2p1g0 (p3p2p1g0_out, g0, p3, p2, p1);
  and p3p2g1 (p3p2g1_out, g1, p2, p3);
  and p3p2p1p0c0 (p3p2p1p0c0_out, c0_t, p0, p1, p2, p3);
  or or_9 (c4_t, g3, p3g2_out, p3p2p1g0_out, p3p2g1_out, p3p2p1p0c0_out);
  not not_3 (not_3_out[0], A0);
  not not_4 (not_3_out[1], A1);
  not not_5 (not_3_out[2], A2);
  not not_6 (not_3_out[3], A3);
  not not_7 (not_3_out[4], A4);
  and p4p3g2 (p4p3g2_out, g2, p4, p3);
  and p4p3p2g1 (p4p3p2g1_out, g1, p4, p3, p2);
  and p4p3p2p1g0 (p4p3p2p1g0_out, p4, p3, p2, g0, p1);
  and p4p3p2p1p0c0 (p4p3p2p1p0c0_out, c0_t, p0, p1, p2, p3, p4);
  Multiplexer #(.select(2), .width(5)) multiplexer_2 (
    .in0({g4, g3, g2, g1, g0}), .in1({o4, o3, o2, o1, o0}), .in2(not_3_out), .in3({s4, s3, s2, s1_t, s0_t}),
    .out({C4, C3, C2, C1, C0}), .sel({q1, q0}));  // open: en
  and p4g3 (p4g3_out, g3, p4);
  or or_10 (C5, g4, p4g3_out, p4p3g2_out, p4p3p2g1_out, p4p3p2p1g0_out, p4p3p2p1p0c0_out);

  // Other names for the same wires on the sheet: CIN = c0_t; S0 = q0; S1 = q1

  // Notes on the sheet:
  //   07
  //   51
  //   40
  //   51
  //   77
  //   77
  //   57
  //   63
  //   43
  //   77
  //   60
  //   51
  //   46
  //   71
  //   32
  //   43
  //   34
  //   50
  //   53
  //   00
  //   07
  //   02
  //   74
  //   04
  //   35
  //   52
  //   52
  //   50
  //   65
  //   46
  //   11
  //   57
  //   Five-bit ALU
endmodule
