// Logisim project 4test.circ as structural Verilog: 1 circuit, main circuit main
module main (
);

  wire Carry, CLK, clock_1_out, counter_1_carry, D0, D1, D2, D3, Enable, Load, not_1_out, Q0, Q1, Q2, Q3;
  wire [5:1] counter_1_q;

  Counter #(.width(6), .max('h24)) counter_1 (
    .Q({counter_1_q[5], Load, D3, counter_1_q[2:1], D0}), .carry(counter_1_carry), .clk(CLK));  // open: load, D, count, clr
  and and_1 (CLK, clock_1_out, not_1_out);
  not not_1 (not_1_out, counter_1_carry);
  Clock clock_1 (.out(clock_1_out));
  TTY #(.rows(1), .cols(37)) tty_1 (.data({2'b10, Carry, Q3, Q2, Q1, Q0}), .clk(CLK));  // open: we, clr
  not not_2 (Enable, counter_1_q[5]);
  or or_1 (D1, Enable, counter_1_q[1]);
  or or_2 (D2, counter_1_q[2], Load);

  // Notes on the sheet:
  //   @ABCDEFGHIJKLMN_@FGFGFGFGN_N_N_N0000
endmodule
