// Logisim project 7test.circ as structural Verilog: 1 circuit, main circuit main
module main (
);

  wire _5_Counter_carry, CLK, clock_1_out, go, p, Reset_out, w;
  wire [2:0] _5_Counter_q;
  wire [5:0] _64_Counter_q;

  TTY #(.rows(33), .cols(5)) tty_1 (.data({6'b011000, p}), .clk(CLK), .we(go), .clr(Reset_out));
  Button Reset (.out(Reset_out));
  // Probe on w
  nand nand_1 (go, _64_Counter_q[0], _64_Counter_q[5]);
  Counter #(.width(3), .max('h4)) _5_Counter (
    .Q(_5_Counter_q), .carry(_5_Counter_carry), .clk(CLK), .clr(Reset_out));  // open: load, D, count
  and and_1 (CLK, clock_1_out, go);
  Clock clock_1 (.out(clock_1_out));
  Counter #(.width(6), .max('h3f), .trigger("falling")) _64_Counter (
    .Q(_64_Counter_q), .clk(_5_Counter_carry), .clr(Reset_out));  // open: load, D, count, carry
  // Probe on _5_Counter_q
  // Probe on _64_Counter_q
  BitSelector #(.width(6)) bitselector_1 (.in(_64_Counter_q), .out(w), .sel(_5_Counter_q));

  // Notes on the sheet:
  //   1  0
  //   1  3
  //   1  5
  //   1  6
  //   1  9
  //   1   10
  //   1  12
  //   1  15
  //   1  17
  //   1  18
  //   1  20
  //   1  23
  //   1  24
  //   1 27
  //   1  29
  //   1  30
  //   24 Gates
endmodule
