// Logisim project alutest.circ as structural Verilog: 1 circuit, main circuit main
module main (
);

  wire A0, A1, A2, A3, A4, B0, B1, B2, B3, B4, C0, C1, C2, C3, C4, C5, CIN, clock_1_out, clock_2_out, go,
       HCLK, not_1_out, reset, S0, S1;
  wire [2:0] multiplexer_1_out;
  wire [6:1] counter_1_q;

  // Probe on {C5, C4, C3}
  // Probe on {C2, C1, C0}
  Multiplexer #(.width(3)) multiplexer_1 (
    .in0({C5, C4, C3}), .in1({C2, C1, C0}), .out(multiplexer_1_out), .sel(HCLK));  // open: en
  // Probe on multiplexer_1_out
  // Probe on {4'b0110, multiplexer_1_out}
  TTY #(.rows(32), .cols(2)) tty_1 (.data({4'b0110, multiplexer_1_out}), .clk(clock_1_out), .we(go), .clr(reset));
  Clock clock_1 (.out(clock_1_out));
  // Probe on {A4, A3, A2, A1, A0, CIN}
  // Probe on {B4, B3, B2, B1, B0}
  // Probe on S1
  Counter #(.width(7), .max('h7f), .ongoal("stay")) counter_1 (
    .Q({counter_1_q, HCLK}), .clk(clock_2_out), .clr(reset));  // open: load, D, count, carry
  Clock clock_2 (.out(clock_2_out));
  // Probe on S0
  not not_1 (not_1_out, HCLK);
  Button u_Reset (.out(reset));
  Random #(.width(13), .seed(34573)) random_1 (
    .clk(not_1_out), .next(go), .out({B4, B3, B2, B1, B0, A4, A3, A2, A1, A0, CIN, S1, S0}), .clr(reset));
  not not_2 (go, counter_1_q[6]);

  // Notes on the sheet:
  //   07
  //   51
  //   40
  //   51
  //   77
  //   77
  //   57
  //   63
  //   43
  //   77
  //   60
  //   51
  //   46
  //   71
  //   32
  //   43
  //   34
  //   50
  //   53
  //   00
  //   07
  //   02
  //   74
  //   04
  //   35
  //   52
  //   52
  //   50
  //   65
  //   46
  //   11
  //   57
endmodule
