// Logisim project CPU.circ as structural Verilog: 17 circuits, main circuit main
module main (
  output [9:0] out_1,
  output [9:0] out_2,
  output [9:0] out_3,
  output [9:0] out_4,
  output [9:0] out_5,
  output [9:0] out_6,
  output [9:0] out_7,
  output ignore,
  output halt
);

  wire and_1_out, button_1_out, button_2_out, CLK, clock_1_out, comparator_1_lt, comparator_2_lt, not_1_out,
       t_ff_1_q, TClock;
  wire [1:0] counter_2_q, Upper_2_bits;
  wire [2:0] cpu_1_decsel, rom_1_data;
  wire [4:0] counter_1_q, PC;
  wire [6:0] adder_1_out, adder_2_out, ASCII, LSB, MiddleBits;
  wire [7:0] multiplexer_1_out;
  wire [9:0] cpu_1_a, cpu_1_b;
  wire [23:0] ram_1_data;

  TTY #(.rows(33), .cols(4)) tty_1 (.data(ASCII), .clk(TClock));  // open: we, clr
  // Probe on out_1
  // Probe on out_5
  Counter #(.width(5), .max('h1f), .ongoal("stay")) counter_1 (
    .Q(counter_1_q), .carry(halt), .clk(CLK));  // open: load, D, count, clr
  // Probe on out_2
  // Probe on out_6
  Multiplexer #(.select(3), .width(10)) multiplexer_1 (
    .in0(out_1), .in1(out_2), .in2(out_3), .in3(out_4), .in4(out_5), .in5(out_6), .in6(out_7),
    .out({Upper_2_bits, multiplexer_1_out}), .sel(rom_1_data));  // open: in7, en
  not not_1 (not_1_out, halt);
  Clock clock_1 (.out(clock_1_out));
  // Probe on out_3
  // Probe on out_7
  ROM #(.addrWidth(5), .dataWidth(3)) rom_1 (.addr(counter_1_q), .data(rom_1_data));  // open: sel
  and and_1 (and_1_out, not_1_out, clock_1_out);
  not not_2 (TClock, and_1_out);
  // Probe on out_4
  T_Flip_Flop t_ff_1 (.clk(and_1_out), .T(1'b1), .Q(t_ff_1_q));  // open: Qn, preset, reset, en
  Comparator #(.width(7)) comparator_1 (
    .a(7'b0111001), .b({3'b011, multiplexer_1_out[3:0]}), .lt(comparator_1_lt));  // open: gt, eq
  Comparator #(.width(7)) comparator_2 (
    .a(7'b0111001), .b({3'b011, multiplexer_1_out[7:4]}), .lt(comparator_2_lt));  // open: gt, eq
  Counter #(.width(2), .max('h3)) counter_2 (.Q(counter_2_q), .clk(TClock));  // open: load, D, count, carry, clr
  T_Flip_Flop t_ff_2 (.clk(t_ff_1_q), .T(1'b1), .Q(CLK));  // open: Qn, preset, reset, en
  Multiplexer #(.width(7), .disabled(0), .enable("false")) multiplexer_2 (
    .in0({3'b011, multiplexer_1_out[3:0]}), .in1(adder_1_out), .out(LSB), .sel(comparator_1_lt));
  Adder #(.width(7)) adder_1 (
    .a({3'b011, multiplexer_1_out[3:0]}), .b(7'b0000111), .out(adder_1_out));  // open: cin, cout
  Multiplexer #(.width(7), .disabled(0), .enable("false")) multiplexer_3 (
    .in0({3'b011, multiplexer_1_out[7:4]}), .in1(adder_2_out), .out(MiddleBits), .sel(comparator_2_lt));
  Adder #(.width(7)) adder_2 (
    .a({3'b011, multiplexer_1_out[7:4]}), .b(7'b0000111), .out(adder_2_out));  // open: cin, cout
  Multiplexer #(.select(2), .width(7)) multiplexer_4 (
    .in0({5'b01100, Upper_2_bits}), .in1(MiddleBits), .in2(LSB), .in3(7'b0100000), .out(ASCII),
    .sel(counter_2_q));  // open: en
  T_Flip_Flop t_ff_3 (.clk(CLK), .T(1'b1), .Q(ignore));  // open: Qn, preset, reset, en
  // Probe on out_1
  // Probe on out_1
  RAM #(.addrWidth(5), .dataWidth(24)) ram_1 (.addr(PC), .data(ram_1_data), .clk(CLK));  // open: sel, ld, clr
  // Probe on ram_1_data[23:19]
  // Probe on out_2
  // Probe on out_2
  // Probe on cpu_1_a
  // Probe on cpu_1_a
  // Probe on cpu_1_a
  // Probe on cpu_1_a
  // Probe on out_3
  // Probe on out_3
  Button button_1 (.out(button_1_out));
  cpu cpu_1 (
    .CLK(CLK), .Input(ram_1_data), .R0(out_1), .R1(out_2), .R2(out_3), .R3(out_4), .R4(out_5), .R5(out_6),
    .R6(out_7), .PC_RST(button_1_out), .Reg_RST(button_2_out), .PC(PC), .A(cpu_1_a), .B(cpu_1_b),
    .DecSel(cpu_1_decsel));
  // Probe on PC
  // Probe on PC
  // Probe on out_4
  // Probe on out_4
  Button button_2 (.out(button_2_out));
  // Probe on cpu_1_b
  // Probe on cpu_1_b
  // Probe on cpu_1_b
  // Probe on cpu_1_b
  // Probe on out_5
  // Probe on out_5
  // Probe on cpu_1_decsel
  // Probe on cpu_1_decsel
  // Probe on out_6
  // Probe on out_6
  // Probe on out_7
  // Probe on out_7

  // Other names for the same wires on the sheet: R0[9:0] = out_1; R1[9:0] = out_2; R2[9:0] = out_3; R3[9:0] = out_4;
  //   R4[9:0] = out_5; R5[9:0] = out_6; R6[9:0] = out_7

  // Notes on the sheet:
  //   DO NOT PUT ANY PINS ON THE main circuit.  (You should not need any anyway.)
  //   0F5
  //   0F5
  //   25A
  //   050
  //   2FF
  //   30A
  //   34F
  //   0F5
  //   1EA
  //   07A
  //   29B
  //   165
  //   10F
  //   0F5
  //   0AA
  //   0AA
  //   05A
  //   00A
  //   0FA
  //   104
  //   0B4
  //   165
  //   165
  //   001
  //   001
  //   000
  //   000
  //   000
  //   000
  //   000
  //   ???
  //   There is no Reset.  Just Ctrl-r, then load test.txt into your RAM, and then Ctrl-k
  //   You must  use the CLK tunnel for the source of your clock.  R0-R6 are the other tunnels you need to connect
  //   contents of rom_1 (hex, n*v repeats v):
  //   0 0 0 1 2 3 4 5 6 2 3 4 5 6 0 0 0 1 3 4 6 3 5 5 8*6
  //   OpCode
endmodule

module cpu (
  input  CLK,
  input  PC_RST,
  input  Reg_RST,
  input  [23:0] Input,
  output [4:0] PC,
  output [2:0] DecSel,
  output [9:0] R0,
  output [9:0] A,
  output [9:0] B,
  output [9:0] R1,
  output [9:0] R2,
  output [9:0] R3,
  output [9:0] R4,
  output [9:0] R5,
  output [9:0] R6
);

  wire not_1_out, PCSel, W, ZFLAG;
  wire [2:0] cu_1_aluctrl, cu_1_asel;
  wire [3:0] BSel;
  wire [6:0] decoder_1_out0;
  wire [9:0] RIN;

  // Probe on R0
  // Probe on R1
  // Probe on R2
  // Probe on R3
  // Probe on R4
  // Probe on R5
  // Probe on R6
  // Probe on Input[23:19]
  not not_1 (not_1_out, CLK);
  CU cu_1 (
    .OpCode(Input[23:19]), .ZFLAG(ZFLAG), .DecSel(DecSel), .ALUCtrl(cu_1_aluctrl), .ASel(cu_1_asel),
    .BSel(BSel), .PCSel(PCSel), .DestAddr(Input[18:16]), .AAddr(Input[15:13]), .BAddr(Input[12:10]), .W(W));
  PC pc_1 (.PCSel(PCSel), .CLK(not_1_out), .DIN(Input[4:0]), .PC(PC), .W(W), .Reset(PC_RST));
  // Probe on Input[4:0]
  Decoder #(.select(3)) decoder_1 (
    .out0(decoder_1_out0[0]), .out1(decoder_1_out0[1]), .out2(decoder_1_out0[2]), .out3(decoder_1_out0[3]),
    .out4(decoder_1_out0[4]), .out5(decoder_1_out0[5]), .out6(decoder_1_out0[6]), .sel(DecSel));  // open: out7, en
  // Probe on cu_1_asel
  // Probe on cu_1_aluctrl
  Multiplexer #(.select(3), .width(10)) multiplexer_1 (
    .in0(R0), .in1(R1), .in2(R2), .in3(R3), .in4(R4), .in5(R5), .in6(R6), .in7({10{1'b0}}), .out(A),
    .sel(cu_1_asel));  // open: en
  // Probe on RIN
  REG_BANK reg_bank_1 (
    .DIN(RIN), .CLK(CLK), .R0(R0), .R1(R1), .R2(R2), .R3(R3), .R4(R4), .R5(R5), .R6(R6), .W(decoder_1_out0),
    .Reset(Reg_RST));
  Multiplexer #(.select(4), .width(10)) multiplexer_2 (
    .in0(R0), .in1(R1), .in2(R2), .in3(R3), .in4(R4), .in5(R5), .in6(R6), .in7({10{1'b0}}), .in8(Input[9:0]),
    .out(B), .sel(BSel));  // open: in9, in10, in11, in12, in13, in14, in15, en
  // Probe on RIN
  ALU alu_1 (.B(B), .CTRL(cu_1_aluctrl), .A(A), .OUT(RIN), .ZFLAG(ZFLAG));  // open: COUT
  // Probe on BSel

  // Other names for the same wires on the sheet: AAddr[2:0] = Input[15:13]; BAddr[2:0] = Input[12:10];
  //   DataI[9:0] = Input[9:0]; DestAddr[2:0] = Input[18:16]; OpCode[4:0] = Input[23:19]

  // Notes on the sheet:
  //   24 bits
endmodule

module CU (
  input  [2:0] DestAddr,
  input  [2:0] BAddr,
  input  [2:0] AAddr,
  input  [4:0] OpCode,
  input  ZFLAG,
  output [2:0] DecSel,
  output [3:0] BSel,
  output [2:0] ASel,
  output [2:0] ALUCtrl,
  output PCSel,
  output W
);

  wire and_1_out, d_selector_1_decsel, not_1_out, not_2_out;
  wire [1:0] a_selector_1_asel, b_selector_1_out_2;

  not not_1 (not_1_out, OpCode[4]);
  nand nand_1 (W, OpCode[4], OpCode[3], OpCode[2], OpCode[1], OpCode[0]);
  Multiplexer #(.select(2), .width(4)) multiplexer_1 (
    .in0({1'b0, BAddr}), .in1(4'b0111), .in2(4'b1000), .out(BSel), .sel(b_selector_1_out_2));  // open: in3, en
  b_selector b_selector_1 (.OpCode(OpCode), .out_2(b_selector_1_out_2));
  not not_2 (not_2_out, OpCode[2]);
  and and_1 (and_1_out, not_1_out, OpCode[3], not_2_out, OpCode[1], OpCode[0]);
  Multiplexer #(.select(2), .width(3)) multiplexer_2 (
    .in0(AAddr), .in1(3'b111), .in2(DestAddr), .out(ASel), .sel(a_selector_1_asel));  // open: in3, en
  a_selector a_selector_1 (.OpCode(OpCode), .ASel(a_selector_1_asel));
  Multiplexer #(.width(3)) multiplexer_3 (
    .in0(DestAddr), .in1(3'b111), .out(DecSel), .sel(d_selector_1_decsel));  // open: en
  d_selector d_selector_1 (.OpCode(OpCode), .DecSel(d_selector_1_decsel));
  Multiplexer multiplexer_4 (.in0(1'b0), .in1(ZFLAG), .out(PCSel), .sel(and_1_out));  // open: en
  alu_selector alu_selector_1 (.OpCode(OpCode), .ALUCtrl(ALUCtrl));

  // Notes on the sheet:
  //   16~18
  //   10~12
  //   13~15
  //   19~23
endmodule

module d_selector (
  input  [4:0] OpCode,
  output DecSel
);

  wire and_1_out, and_2_out;

  and and_1 (and_1_out, OpCode[3], OpCode[2]);
  and and_2 (and_2_out, OpCode[3], OpCode[1], OpCode[0]);
  or or_1 (DecSel, and_1_out, and_2_out);
endmodule

module a_selector (
  input  [4:0] OpCode,
  output [1:0] ASel
);

  wire not_1_out, not_2_out, not_3_out, not_4_out, not_5_out;

  not not_1 (not_1_out, OpCode[4]);
  not not_2 (not_2_out, OpCode[2]);
  not not_3 (not_3_out, OpCode[0]);
  not not_4 (not_4_out, OpCode[4]);
  not not_5 (not_5_out, OpCode[2]);
  and _01010 (ASel[0], not_1_out, OpCode[3], not_2_out, OpCode[1], not_3_out);
  and _01011 (ASel[1], not_4_out, OpCode[3], not_5_out, OpCode[1], OpCode[0]);

  // Notes on the sheet:
  //   a0
  //   a1
endmodule

module b_selector (
  input  [4:0] OpCode,
  output [1:0] out_2
);

  wire _21_n20_out, _22_20_19_out, _22_n19_out, _22_n20_out, n22_20_n19_out, not_1_out, not_2_out, not_3_out,
       not_4_out, not_5_out;

  and _22_n20 (_22_n20_out, OpCode[3], not_1_out);
  not not_1 (not_1_out, OpCode[1]);
  and _22_n19 (_22_n19_out, OpCode[3], not_2_out);
  not not_2 (not_2_out, OpCode[0]);
  and _21_n20 (_21_n20_out, OpCode[2], not_3_out);
  not not_3 (not_3_out, OpCode[1]);
  not not_4 (not_4_out, OpCode[3]);
  and n22_20_n19 (n22_20_n19_out, not_4_out, OpCode[1], not_5_out);
  not not_5 (not_5_out, OpCode[0]);
  and _22_20_19 (_22_20_19_out, OpCode[3], OpCode[1], OpCode[0]);
  or b1 (out_2[1], _22_n20_out, _22_n19_out);
  or b0 (out_2[0], _21_n20_out, n22_20_n19_out, _22_20_19_out);
endmodule

module alu_selector (
  input  [4:0] OpCode,
  output [2:0] ALUCtrl
);

  wire _21_19_out, _21_20_out, _21_n19_out, _21_n20_out, _22_20_out, _22_n19_2_out, _22_n19_out,
       _22_n20_19_out, n21_20_out, n22_n21_19_out, not_1_out, not_2_out, not_3_out, not_4_out;

  not not_1 (not_1_out, OpCode[3]);
  not not_2 (not_2_out, OpCode[2]);
  not not_3 (not_3_out, OpCode[1]);
  not not_4 (not_4_out, OpCode[0]);
  and _21_19 (_21_19_out, OpCode[2], OpCode[0]);
  and _21_20 (_21_20_out, OpCode[2], OpCode[1]);
  and _22_n20_19 (_22_n20_19_out, OpCode[3], not_3_out, OpCode[0]);
  and _21_n19 (_21_n19_out, OpCode[2], not_4_out);
  and _22_n19 (_22_n19_out, OpCode[3], not_4_out);
  and n21_20 (n21_20_out, not_2_out, OpCode[1]);
  and n22_n21_19 (n22_n21_19_out, not_1_out, not_2_out, OpCode[0]);
  and _21_n20 (_21_n20_out, OpCode[2], not_3_out);
  and _22_n19_2 (_22_n19_2_out, OpCode[3], not_4_out);
  and _22_20 (_22_20_out, OpCode[3], OpCode[1]);
  or a2 (ALUCtrl[2], _21_19_out, _21_20_out, _22_n20_19_out);
  or a1 (ALUCtrl[1], _21_n19_out, _22_n19_out, n21_20_out);
  or a0 (ALUCtrl[0], n22_n21_19_out, _21_n20_out, _22_n19_2_out, _22_20_out);

  // Notes on the sheet:
  //   22
  //   21
  //   20
  //   19
endmodule

module ALU (
  input  [9:0] B,
  input  [2:0] CTRL,
  input  [9:0] A,
  output COUT,
  output ZFLAG,
  output [9:0] OUT
);

  wire not_2_out, not_3_out, not_4_out, not_5_out, sub;
  wire [1:0] ctrl1, shift;
  wire [9:0] multiplexer_1_out, not_1_out, result;

  Multiplexer #(.width(10)) multiplexer_1 (.in0(B), .in1(not_1_out), .out(multiplexer_1_out), .sel(sub));  // open: en
  assign not_1_out = ~B;  // NOT_Gate not_1, 10 bits wide
  or or_1 (ZFLAG, result[0], result[1], result[2], result[3], result[4], result[5], result[6], result[7], result[8], result[9]);
  Multiplexer #(.select(2), .width(10)) multiplexer_2 (
    .in0(result), .in1({1'b0, result[9:1]}), .in2({result[8:0], 1'b0}), .out(OUT), .sel(shift));  // open: in3, en
  alu_factory alu_factory_1 (.SUB(sub), .COUT(COUT), .A(A), .B(multiplexer_1_out), .CTRL(ctrl1), .OUT(result));
  or q0 (ctrl1[0], CTRL[0], CTRL[2]);
  or q1 (ctrl1[1], CTRL[1], CTRL[2]);
  not not_2 (not_2_out, CTRL[0]);
  not not_3 (not_3_out, CTRL[1]);
  not not_4 (not_4_out, CTRL[0]);
  not not_5 (not_5_out, CTRL[1]);
  and u_sub (sub, not_2_out, not_3_out, CTRL[2]);
  and s0 (shift[0], not_4_out, CTRL[1], CTRL[2]);
  and s1 (shift[1], CTRL[0], not_5_out, CTRL[2]);

  // Notes on the sheet:
  //   SRL
  //   SLL
  //   shift:
  //   00 = normal
  //   01 = SRL
  //   10 = SLL
  //   zero = 0
  //   else = 1
  //   q0 = Q0 + Q2
  //   q1 = Q1 + Q2
  //   sub = !Q0!Q1Q2
  //   s0 = !Q0Q1Q2
  //   s1 = Q0!Q1Q2
  //   00 = AND
  //   ctrl1:
  //   01 = OR
  //   10 = NOT
  //   11 = ADD
  //   shift:
  //   00 = normal
  //   01 = SRL
  //   10 = SLL
endmodule

module alu_factory (
  input  [9:0] A,
  input  [9:0] B,
  input  [1:0] CTRL,
  input  SUB,
  output [9:0] OUT,
  output COUT
);

  wire c1, c2, c3, c4, c5, c6, c7, c8, c9, g0, g1, g2, g3, g4, g5, g6, g7, g8, g9, p0, p1, p2, p3, p4, p5,
       p6, p7, p8, p9;

  _1_bit_alu u_1_bit_alu_1 (.A(A[0]), .B(B[0]), .CARRY(SUB), .OUT(OUT[0]), .P(p0), .G(g0), .CTRL(CTRL));
  _1_bit_alu u_1_bit_alu_2 (.A(A[1]), .B(B[1]), .CARRY(c1), .OUT(OUT[1]), .P(p1), .G(g1), .CTRL(CTRL));
  _1_bit_alu u_1_bit_alu_3 (.A(A[2]), .B(B[2]), .CARRY(c2), .OUT(OUT[2]), .P(p2), .G(g2), .CTRL(CTRL));
  _1_bit_alu u_1_bit_alu_4 (.A(A[3]), .B(B[3]), .CARRY(c3), .OUT(OUT[3]), .P(p3), .G(g3), .CTRL(CTRL));
  _1_bit_alu u_1_bit_alu_5 (.A(A[4]), .B(B[4]), .CARRY(c4), .OUT(OUT[4]), .P(p4), .G(g4), .CTRL(CTRL));
  _1_bit_alu u_1_bit_alu_6 (.A(A[5]), .B(B[5]), .CARRY(c5), .OUT(OUT[5]), .P(p5), .G(g5), .CTRL(CTRL));
  _1_bit_alu u_1_bit_alu_7 (.A(A[6]), .B(B[6]), .CARRY(c6), .OUT(OUT[6]), .P(p6), .G(g6), .CTRL(CTRL));
  _1_bit_alu u_1_bit_alu_8 (.A(A[7]), .B(B[7]), .CARRY(c7), .OUT(OUT[7]), .P(p7), .G(g7), .CTRL(CTRL));
  _1_bit_alu u_1_bit_alu_9 (.A(A[8]), .B(B[8]), .CARRY(c8), .OUT(OUT[8]), .P(p8), .G(g8), .CTRL(CTRL));
  _1_bit_alu u_1_bit_alu_10 (.A(A[9]), .B(B[9]), .CARRY(c9), .OUT(OUT[9]), .P(p9), .G(g9), .CTRL(CTRL));
  _5_bit_clu u_5_bit_clu_1 (
    .c1(c1), .c2(c2), .c3(c3), .c4(c4), .cout(c5), .cin(SUB), .p0(p0), .g0(g0), .p1(p1), .g1(g1), .p2(p2),
    .g2(g2), .p3(p3), .g3(g3), .p4(p4), .g4(g4));
  _5_bit_clu u_5_bit_clu_2 (
    .c1(c6), .c2(c7), .c3(c8), .c4(c9), .cout(COUT), .cin(c5), .p0(p5), .g0(g5), .p1(p6), .g1(g6), .p2(p7),
    .g2(g7), .p3(p8), .g3(g8), .p4(p9), .g4(g9));

  // Notes on the sheet:
  //   alu0
  //   alu1
  //   alu2
  //   alu3
  //   alu4
  //   alu5
  //   alu6
  //   alu7
  //   alu8
  //   alu9
endmodule

module _5_bit_clu (
  input  cin,
  input  p0,
  input  g0,
  input  p1,
  input  g1,
  input  p2,
  input  g2,
  input  p3,
  input  g3,
  input  p4,
  input  g4,
  output c1,
  output c2,
  output c3,
  output c4,
  output cout
);

  wire p0c0_out, p1g0_out, p1p0c0_out, p2g1_out, p2p1g0_out, p2p1p0c0_out, p3g2_out, p3p2g1_out,
       p3p2p1g0_out, p3p2p1p0c0_out, p4g3_out, p4p3g2_out, p4p3p2g1_out, p4p3p2p1g0_out, p4p3p2p1p0c0_out;

  and p0c0 (p0c0_out, p0, cin);
  and p1g0 (p1g0_out, p1, g0);
  and p1p0c0 (p1p0c0_out, p1, p0, cin);
  and p2g1 (p2g1_out, p2, g1);
  and p2p1g0 (p2p1g0_out, p2, p1, g0);
  and p2p1p0c0 (p2p1p0c0_out, p2, p1, p0, cin);
  and p3g2 (p3g2_out, p3, g2);
  and p3p2g1 (p3p2g1_out, p3, p2, g1);
  and p3p2p1g0 (p3p2p1g0_out, p3, p2, p1, g0);
  and p3p2p1p0c0 (p3p2p1p0c0_out, p3, p2, p1, p0, cin);
  and p4g3 (p4g3_out, p4, g3);
  and p4p3g2 (p4p3g2_out, p4, p3, g2);
  and p4p3p2g1 (p4p3p2g1_out, p4, p3, p2, g1);
  and p4p3p2p1g0 (p4p3p2p1g0_out, p4, p3, p2, p1, g0);
  and p4p3p2p1p0c0 (p4p3p2p1p0c0_out, p4, p3, p2, p1, p0, cin);
  or or_1 (c1, g0, p0c0_out);
  or or_2 (c2, g1, p1g0_out, p1p0c0_out);
  or or_3 (c3, g2, p2g1_out, p2p1g0_out, p2p1p0c0_out);
  or or_4 (c4, g3, p3g2_out, p3p2g1_out, p3p2p1g0_out, p3p2p1p0c0_out);
  or or_5 (cout, g4, p4g3_out, p4p3g2_out, p4p3p2g1_out, p4p3p2p1g0_out, p4p3p2p1p0c0_out);
endmodule

module _1_bit_alu (
  input  [1:0] CTRL,
  input  A,
  input  B,
  input  CARRY,
  output P,
  output OUT,
  output G
);

  wire \not , \or , sum;

  not not_1 (\not , A);
  or or_1 (\or , B, A);
  xor xor_1 (P, A, B);
  and and_1 (G, A, B);
  xor xor_2 (sum, P, CARRY);
  Multiplexer #(.select(2)) multiplexer_1 (
    .in0(G), .in1(\or ), .in2(\not ), .in3(sum), .out(OUT), .sel(CTRL));  // open: en

  // Other names for the same wires on the sheet: and = G

  // Notes on the sheet:
  //   00 = AND
  //   CTRL:
  //   01 = OR
  //   10 = NOT
  //   11 = ADD
endmodule

module REG_BANK (
  input  [6:0] W,
  input  [9:0] DIN,
  input  CLK,
  input  Reset,
  output [9:0] R0,
  output [9:0] R1,
  output [9:0] R2,
  output [9:0] R3,
  output [9:0] R4,
  output [9:0] R5,
  output [9:0] R6
);

  _10_bit_reg u_R0 (.CLK(CLK), .W(W[0]), .DIN(DIN), .DOUT(R0), .Reset(Reset));
  _10_bit_reg u_R1 (.CLK(CLK), .W(W[1]), .DIN(DIN), .DOUT(R1), .Reset(Reset));
  _10_bit_reg u_R2 (.CLK(CLK), .W(W[2]), .DIN(DIN), .DOUT(R2), .Reset(Reset));
  _10_bit_reg u_R3 (.CLK(CLK), .W(W[3]), .DIN(DIN), .DOUT(R3), .Reset(Reset));
  _10_bit_reg u_R4 (.CLK(CLK), .W(W[4]), .DIN(DIN), .DOUT(R4), .Reset(Reset));
  _10_bit_reg u_R5 (.CLK(CLK), .W(W[5]), .DIN(DIN), .DOUT(R5), .Reset(Reset));
  _10_bit_reg u_R6 (.CLK(CLK), .W(W[6]), .DIN(DIN), .DOUT(R6), .Reset(Reset));
endmodule

module _10_bit_reg (
  input  CLK,
  input  W,
  input  Reset,
  input  [9:0] DIN,
  output [9:0] DOUT
);

  D_Flip_Flop DFF0 (.clk(CLK), .D(DIN[0]), .Q(DOUT[0]), .en(W), .reset(Reset));  // open: Qn, preset
  D_Flip_Flop DFF1 (.clk(CLK), .D(DIN[1]), .Q(DOUT[1]), .en(W), .reset(Reset));  // open: Qn, preset
  D_Flip_Flop DFF2 (.clk(CLK), .D(DIN[2]), .Q(DOUT[2]), .en(W), .reset(Reset));  // open: Qn, preset
  D_Flip_Flop DFF3 (.clk(CLK), .D(DIN[3]), .Q(DOUT[3]), .en(W), .reset(Reset));  // open: Qn, preset
  D_Flip_Flop DFF4 (.clk(CLK), .D(DIN[4]), .Q(DOUT[4]), .en(W), .reset(Reset));  // open: Qn, preset
  D_Flip_Flop DFF5 (.clk(CLK), .D(DIN[5]), .Q(DOUT[5]), .en(W), .reset(Reset));  // open: Qn, preset
  D_Flip_Flop DFF6 (.clk(CLK), .D(DIN[6]), .Q(DOUT[6]), .en(W), .reset(Reset));  // open: Qn, preset
  D_Flip_Flop DFF7 (.clk(CLK), .D(DIN[7]), .Q(DOUT[7]), .en(W), .reset(Reset));  // open: Qn, preset
  D_Flip_Flop DFF8 (.clk(CLK), .D(DIN[8]), .Q(DOUT[8]), .en(W), .reset(Reset));  // open: Qn, preset
  D_Flip_Flop DFF9 (.clk(CLK), .D(DIN[9]), .Q(DOUT[9]), .en(W), .reset(Reset));  // open: Qn, preset
endmodule

module PC (
  input  [4:0] DIN,
  input  PCSel,
  input  Reset,
  input  CLK,
  input  W,
  output [4:0] PC
);

  wire [4:0] multiplexer_1_out, pc_adder_1_out;

  pc_adder pc_adder_1 (.A(PC), .B(multiplexer_1_out), .OUT(pc_adder_1_out));  // open: COUT
  _5_bit_counter u_5_bit_counter_1 (.DOUT(PC), .CLK(CLK), .W(W), .DIN(pc_adder_1_out), .Reset(Reset));
  Multiplexer #(.width(5)) multiplexer_1 (.in0(5'b00001), .in1(DIN), .out(multiplexer_1_out), .sel(PCSel));  // open: en

  // Other names for the same wires on the sheet: sel = PCSel
endmodule

module pc_adder (
  input  [4:0] A,
  input  [4:0] B,
  output [4:0] OUT,
  output COUT
);

  wire c1, c2, c3, c4, g0, g1, g2, g3, g4, p0, p1, p2, p3, p4;

  _1_bit_alu u_1_bit_alu_1 (.A(A[0]), .B(B[0]), .CARRY(1'b0), .OUT(OUT[0]), .P(p0), .G(g0), .CTRL(2'b11));
  _1_bit_alu u_1_bit_alu_2 (.A(A[1]), .B(B[1]), .CARRY(c1), .OUT(OUT[1]), .P(p1), .G(g1), .CTRL(2'b11));
  _1_bit_alu u_1_bit_alu_3 (.A(A[2]), .B(B[2]), .CARRY(c2), .OUT(OUT[2]), .P(p2), .G(g2), .CTRL(2'b11));
  _1_bit_alu u_1_bit_alu_4 (.A(A[3]), .B(B[3]), .CARRY(c3), .OUT(OUT[3]), .P(p3), .G(g3), .CTRL(2'b11));
  _1_bit_alu u_1_bit_alu_5 (.A(A[4]), .B(B[4]), .CARRY(c4), .OUT(OUT[4]), .P(p4), .G(g4), .CTRL(2'b11));
  _5_bit_clu u_5_bit_clu_1 (
    .c1(c1), .c2(c2), .c3(c3), .c4(c4), .cout(COUT), .cin(1'b0), .p0(p0), .g0(g0), .p1(p1), .g1(g1), .p2(p2),
    .g2(g2), .p3(p3), .g3(g3), .p4(p4), .g4(g4));

  // Notes on the sheet:
  //   alu0
  //   alu1
  //   alu2
  //   alu3
  //   alu4
endmodule

module _5_bit_counter (
  input  CLK,
  input  W,
  input  Reset,
  input  [4:0] DIN,
  output [4:0] DOUT
);

  D_Flip_Flop DFF0 (.clk(CLK), .D(DIN[0]), .Q(DOUT[0]), .en(W), .reset(Reset));  // open: Qn, preset
  D_Flip_Flop DFF1 (.clk(CLK), .D(DIN[1]), .Q(DOUT[1]), .en(W), .reset(Reset));  // open: Qn, preset
  D_Flip_Flop DFF2 (.clk(CLK), .D(DIN[2]), .Q(DOUT[2]), .en(W), .reset(Reset));  // open: Qn, preset
  D_Flip_Flop DFF3 (.clk(CLK), .D(DIN[3]), .Q(DOUT[3]), .en(W), .reset(Reset));  // open: Qn, preset
  D_Flip_Flop DFF4 (.clk(CLK), .D(DIN[4]), .Q(DOUT[4]), .en(W), .reset(Reset));  // open: Qn, preset
endmodule

module ctr_unit (
  input  CLK,
  input  T,
  input  D,
  input  W,
  output Q
);

  wire multiplexer_1_out, xor_1_out;

  xor xor_1 (xor_1_out, T, Q);
  Multiplexer multiplexer_1 (.in0(xor_1_out), .in1(D), .out(multiplexer_1_out), .sel(W));  // open: en
  D_Flip_Flop d_ff_1 (.clk(CLK), .D(multiplexer_1_out), .Q(Q));  // open: Qn, preset, en, reset
endmodule
